# Fritzing sketch Controller Board (saved by Fritzing 0.9.3b)
perfboards: 1

parts:
  Part1 = Arduino Nano (Rev3.0) (ICSP)  # not connected
  Part2 = NRF24L01+ Breakout Board
  BAT1 = BC9VPC [package=bc9vpc]  # not connected
  C1 = Electrolytic Capacitor [capacitance=10µF voltage=10V package="100 mil [THT, electrolytic]"]
  Part3 = Tri-Axis Gyro Breakout - L3G4200D  # not connected

nets:
  N1: Part2.GND, C1.-
  N2: Part2.VCC, C1.+
