# Fritzing sketch Car Board (saved by Fritzing 0.9.3b)
perfboards: 1

parts:
  Arduino_Microcontroller = Arduino Nano (Rev3.0) (ICSP)
  RF_Transceiver = NRF24L01+ Breakout Board
  IC1 = L293D [package=THT]
  M1 = DC Motor
  M2 = DC Motor
  BAT1 = BC9VPC [package=bc9vpc]
  C1 = Electrolytic Capacitor [capacitance=10µF voltage=10V package="100 mil [THT, electrolytic]"]

nets:
  GND: Arduino_Microcontroller.GND, RF_Transceiver.GND, IC1.0V, BAT1.V-, C1.-
  N1: Arduino_Microcontroller.D2, IC1.In_2
  N2: Arduino_Microcontroller.D3, IC1.In_1
  N3: Arduino_Microcontroller.D4, IC1.In_4
  N4: Arduino_Microcontroller.D5, IC1.Enable_1
  N5: Arduino_Microcontroller.D6, IC1.Enable_2
  N6: Arduino_Microcontroller.D7, RF_Transceiver.CE
  N7: Arduino_Microcontroller.D8, RF_Transceiver.CS
  N8: Arduino_Microcontroller.D9, IC1.In_3
  N9: Arduino_Microcontroller.D11/MOSI, RF_Transceiver.MOSI
  N10: Arduino_Microcontroller.D12/MISO, RF_Transceiver.MISO
  N11: Arduino_Microcontroller.VIN, IC1.+Vmotor, BAT1.V+
  3V3: Arduino_Microcontroller.3V3, RF_Transceiver.VCC, C1.+
  N12: Arduino_Microcontroller.D13/SCK, RF_Transceiver.SCK
  N13: IC1.Out_1_(_Controlled_by_Enable_1_), M2.pin_2
  N14: IC1.Out_2_(_Controlled_by_Enable_1_), M2.pin_1
  N15: IC1.Out_3_(_Controlled_by_Enable_2_), M1.pin_2
  N16: IC1.Out_4_(_Controlled_by_Enable_2_), M1.pin_1
