# Fritzing sketch Controller Board (saved by Fritzing 0.9.3b)
perfboards: 1

parts:
  Part1 = Arduino Nano (Rev3.0) (ICSP)
  BAT1 = BC9VPC [package=bc9vpc]
  C1 = Electrolytic Capacitor [capacitance=10µF voltage=10V package="100 mil [THT, electrolytic]"]
  Gyro = Tri-Axis Gyro Breakout - L3G4200D
  RF_Transceiver = NRF24L01+ Breakout Board

nets:
  GND: Part1.GND, BAT1.V-, C1.-, Gyro.GND, RF_Transceiver.GND
  N1: Part1.D7, RF_Transceiver.CE
  N2: Part1.D8, RF_Transceiver.CS
  N3: Part1.D11/MOSI, RF_Transceiver.MOSI
  N4: Part1.D12/MISO, RF_Transceiver.MISO
  N5: Part1.VIN, BAT1.V+
  5V: Part1.5V, Gyro.VCC
  N6: Part1.A5, Gyro.SCL
  N7: Part1.A4, Gyro.SDA
  3V3: Part1.3V3, C1.+, RF_Transceiver.VCC
  N8: Part1.D13/SCK, RF_Transceiver.SCK
